# Fritzing sketch schematic (saved by Fritzing 0.9.3b)
breadboards: 1

parts:
  BMP280 = Adafruit_BMP280
  PIR = PIR sensor
  DHT-OUT = DHT22 Humidity and Temperature Sensor [part_number=DHT-OUT]
  SSD1306 = OLED 0.96" 128x64 I2C SSD1306
  DHT-IN = DHT22 Humidity and Temperature Sensor [part_number=DHT-IN]
  U1 = NodeMCU V1.0

nets:
  VDD: BMP280.VIN, PIR.VDD, DHT-OUT.VDD, SSD1306.VCC, DHT-IN.VDD, U1.3V3
  GND: BMP280.GND, PIR.GND, DHT-OUT.NULL, DHT-OUT.GND, SSD1306.GND, DHT-IN.GND, U1.GND
  N1: BMP280.SCK/SCL, SSD1306.SCL, U1.D6
  N2: BMP280.SDI/SDA, SSD1306.SCA, U1.D7
  N3: PIR.SIG, U1.D1

custom parts:
  Adafruit_BMP280: Bosch has stepped up their game with their new BMP280 sensor, an environmental sensor with temperature, barometric pressure that is the next generation upgrade to the BMP085/BMP180/BMP183. This sensor is great for all sorts of weather sensing and can even be used in both I2C and SPI! This precision sensor from Bosch is the best low-cost, precision sensing solution for measuring barometric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
  NodeMCU V1.0: ESP8266 based NodeMCU
