# Fritzing sketch schematic (saved by Fritzing 0.9.3b)
breadboards: 1

parts:
  NodeMCU = ESP8266 NodeMCU LoLin module
  LED = smd LED [color="Blue (505nm)" package="0805 [SMD]"]
  R1 = Resistor [tolerance=±5% resistance=100 package="1206 [SMD]"]
  R2 = Resistor [tolerance=±5% resistance=470 package="1206 [SMD]"]
  Q1 = TRANSISTOR_NPN [package=to-92-ammo]
  Buzzer = Piezo Speaker
  DS18B20 = Header 3 [package=molex-1x3_lock]
  D1 = Rectifier Diode [part_number=1N4001 package="Melf DO-213 AB [SMD]"]

nets:
  N1: NodeMCU.D2, R2.Pin_0
  N2: NodeMCU.3V3, R1.Pin_0, Buzzer.pin1, DS18B20.3, D1.cathode
  N3: NodeMCU.GND, Q1.E, DS18B20.1
  N4: NodeMCU.D5, LED.cathode
  N5: NodeMCU.D7, DS18B20.2
  N6: LED.anode, R1.Pin_1
  N7: R2.Pin_1, Q1.B
  N8: Q1.C, Buzzer.pin2, D1.anode

custom parts:
  ESP8266 NodeMCU LoLin module: ESP8266 based NodeMCU
